// Logisim project circuit.circ as structural Verilog: 1 circuit, main circuit main
module main (
  input  E0,
  input  E1,
  input  C,
  output halt,
  output Ec
);


  assign Ec = 1'b1;
  assign halt = 1'b1;
endmodule
